# Fritzing sketch S3feather_DS3231 (saved by Fritzing 1.0.1rc)
breadboards: 1

parts:
  ZS-042_RTC1 = ZS-042 RTC Module  # not connected
  A2 = featherS3

nets:
  N1: A2.Pin_4, A2.Pin_17, A2.Pin_20, A2.Pin_38
  N2: A2.Pin_29, A2.Pin_34, A2.Pin_35

custom parts:
  featherS3: FeatherS3 is the latest in our super popular ESP32 based Feather boards.
