# Fritzing sketch S3feather_MCP23017 (saved by Fritzing 1.0.1rc)
breadboards: 1

parts:
  IC1 = MCP23017 I2C I/O Expander
  R1 = Resistor [tolerance=±5% power=0.25 resistance=10k package=THT]
  R2 = Resistor [tolerance=±5% power=0.25 resistance=10k package=THT]
  R3 = Resistor [tolerance=±5% power=0.25 resistance=10k package=THT]
  LED2 = LED - 5mm [color="Red (633nm)" current=0.030 package="5 mm [THT]"]
  LED1 = LED - 5mm [color="Blue (470nm)" current=0.030 package="5 mm [THT]"]
  Switch1 = Pushbutton [package="[SMD]"]
  Switch2 = Pushbutton [package="[SMD]"]
  A1 = featherS3

nets:
  N1: IC1.GPB0, LED2.anode
  N2: IC1.GPB1, LED1.anode
  N3: IC1.VDD, R1.Pin_1, R2.Pin_1, R3.Pin_0, A1.Pin_2
  N4: IC1.VSS, IC1.A0, IC1.A1, IC1.A2, LED2.cathode, LED1.cathode, Switch1.Pin_1, Switch1.Pin_2, Switch2.Pin_1, Switch2.Pin_2, A1.Pin_4, A1.Pin_17, A1.Pin_33, A1.Pin_38
  N5: IC1.SCL, R1.Pin_0, A1.Pin_22
  N6: IC1.SDA, R2.Pin_0, A1.Pin_21
  N7: IC1.RESET, R3.Pin_1
  N8: IC1.GPA4, Switch1.Pin_3, Switch1.Pin_4
  N9: IC1.GPA7, Switch2.Pin_3, Switch2.Pin_4
  N10: A1.Pin_29, A1.Pin_34, A1.Pin_35

custom parts:
  MCP23017 I2C I/O Expander: The MCP23017 uses two i2c pins (these can be shared with other i2c devices), and in exchange gives you 16 general purpose pins. You can set each of 16 pins to be input, output, input with a pullup or open drain. There's even the ability to get an interrupt via an external pin when any of the inputs change so you don't have to keep polling the chip.
  featherS3: FeatherS3 is the latest in our super popular ESP32 based Feather boards.
