# Fritzing sketch S3feather_MCP9808 (saved by Fritzing 1.0.1rc)
breadboards: 1

parts:
  ZS-042_RTC1 = ZS-042 RTC Module  # not connected
  Part3 = MCP9808 High Accuracy I2C Temperature Sensor [part_number=1782]
  A2 = featherS3

nets:
  N1: Part3.VDD, A2.Pin_2
  N2: Part3.GND, A2.Pin_4, A2.Pin_17, A2.Pin_20, A2.Pin_28, A2.Pin_33, A2.Pin_38
  N3: Part3.SCL, A2.Pin_22
  N4: Part3.SDA, A2.Pin_21
  N5: A2.Pin_29, A2.Pin_34, A2.Pin_35

custom parts:
  MCP9808 High Accuracy I2C Temperature Sensor: This I2C digital temperature sensor is one of the more accurate/precise we've ever seen, with a typical accuracy of ±0.25°C over the sensor's -40°C to +125°C range and precision of +0.0625°C. They work great with any microcontroller using standard i2c. There are 3 address pins so you can connect up to 8 to a single I2C bus without address collisions. Best of all, a wide voltage range makes is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
  featherS3: FeatherS3 is the latest in our super popular ESP32 based Feather boards.
