# Fritzing sketch S3feather_light_freq (saved by Fritzing 1.0.1rc)
breadboards: 1

parts:
  CD4017B = IC, DIP package, 16 pins [chip_label=CD4017B]
  CD4017B1 = IC, DIP package, 16 pins [chip_label=CD4017B]
  LED1 = DUO LED RG [package="5 mm [THT]"]
  A2 = featherS3

nets:
  N1: CD4017B.pin8, CD4017B1.pin8, A2.Pin_5
  N2: CD4017B.pin12, CD4017B1.pin14, A2.Pin_21
  N3: CD4017B.pin13, CD4017B.pin15, CD4017B.pin16, CD4017B1.pin13, CD4017B1.pin15, CD4017B1.pin16, LED1.Vin
  N4: CD4017B.pin14, LED1.Vout
  N5: A2.Pin_4, A2.Pin_33
  N6: A2.Pin_35, A2.Pin_36

notes:
  R1
  Vdata
  3V3
  GND
  RTH2

custom parts:
  DUO LED RG: A 5mm DUO-color LED with red and green inside. Pin order: red - com. cathode - green
  featherS3: FeatherS3 is the latest in our super popular ESP32 based Feather boards.
