# Fritzing sketch S3feather_sdcard2 (saved by Fritzing 1.0.1rc)
breadboards: 1

parts:
  microSD_Transflash2 = SparkFun - microSD Transflash
  A2 = featherS3

nets:
  N1: microSD_Transflash2.DO, A2.Pin_13
  N2: microSD_Transflash2.GND, A2.Pin_4, A2.Pin_17, A2.Pin_20, A2.Pin_38
  N3: microSD_Transflash2.SCK, A2.Pin_11
  N4: microSD_Transflash2.VCC, A2.Pin_2
  N5: microSD_Transflash2.DI, A2.Pin_12
  N6: microSD_Transflash2.CS, A2.Pin_25
  N7: A2.Pin_29, A2.Pin_34, A2.Pin_35

custom parts:
  featherS3: FeatherS3 is the latest in our super popular ESP32 based Feather boards.
