# Fritzing sketch S3feather_switch (saved by Fritzing 1.0.1rc)
breadboards: 1

parts:
  Switch = Pushbutton [package="[SMD]"]
  Relay = mystery part, 4 pins [chip_label=SSR]
  Resistor = Resistor [tolerance=±5% resistance=100 power=0.25W package=THT]
  LED = LED - 5mm [color="Blue (430nm)" current=0.030A package="5 mm [THT]"]
  A1 = featherS3

nets:
  N1: Switch.Pin_1, Switch.Pin_2, Relay.pin2, A1.Pin_4, A1.Pin_28, A1.Pin_33, A1.Pin_38
  N2: Switch.Pin_3, Switch.Pin_4, A1.Pin_23
  N3: Relay.pin1, A1.Pin_29, A1.Pin_35, A1.Pin_36
  N4: Relay.pin4, Resistor.Pin_0
  N5: Resistor.Pin_1, LED.cathode
  N6: LED.anode, A1.Pin_2

custom parts:
  featherS3: FeatherS3 is the latest in our super popular ESP32 based Feather boards.
