# Fritzing sketch S3feather_switch_LED (saved by Fritzing 1.0.1rc)
breadboards: 1

parts:
  Switch = Pushbutton [package="[SMD]"]
  Resistor = Resistor [tolerance=±5% resistance=100 power=0.25W package=THT]
  LED = LED - 5mm [color="Blue (430nm)" current=0.030A package="5 mm [THT]"]
  A2 = featherS3

nets:
  N1: Switch.Pin_1, Switch.Pin_2, Resistor.Pin_0, A2.Pin_4, A2.Pin_28, A2.Pin_33
  N2: Switch.Pin_3, Switch.Pin_4, A2.Pin_23
  N3: Resistor.Pin_1, LED.cathode
  N4: LED.anode, A2.Pin_2
  N5: A2.Pin_29, A2.Pin_35, A2.Pin_36

custom parts:
  featherS3: FeatherS3 is the latest in our super popular ESP32 based Feather boards.
