# Fritzing sketch S3feather_thermistor (saved by Fritzing 1.0.1rc)
breadboards: 1

parts:
  R1 = Resistor [tolerance=±5% resistance=100k package="2512 [SMD]"]
  R3 = Temperature Sensor (Thermistor) [thermistor_type=NTC package=THT]
  A2 = featherS3

nets:
  N1: R1.Pin_0, R3.pin_1, A2.Pin_5
  N2: R1.Pin_1, A2.Pin_2
  N3: R3.pin_0, A2.Pin_4, A2.Pin_17, A2.Pin_20, A2.Pin_38
  N4: A2.Pin_29, A2.Pin_34, A2.Pin_35

notes:
  R1
  Vdata
  3V3
  GND
  RTH2

custom parts:
  featherS3: FeatherS3 is the latest in our super popular ESP32 based Feather boards.
