# Fritzing sketch S3feather_tsl237 (saved by Fritzing 1.0.1rc)
breadboards: 1

parts:
  CD4017B1 = IC, DIP package, 16 pins [chip_label=CD4017B]
  LED2 = DUO LED RG [package="5 mm [THT]"]
  A2 = featherS3

nets:
  N1: CD4017B1.pin8, CD4017B1.pin13, CD4017B1.pin15, LED2.GND, A2.Pin_4, A2.Pin_17, A2.Pin_38
  N2: CD4017B1.pin12, A2.Pin_22
  N3: CD4017B1.pin14, LED2.Vout
  N4: CD4017B1.pin16, LED2.Vin, A2.Pin_2
  N5: A2.Pin_19, A2.Pin_20
  N6: A2.Pin_29, A2.Pin_34, A2.Pin_35
  N7: A2.Pin_30, A2.Pin_36

notes:
  GND
  Vout
  Vin
  TSL237
  Divider/counter

custom parts:
  DUO LED RG: A 5mm DUO-color LED with red and green inside. Pin order: red - com. cathode - green
  featherS3: FeatherS3 is the latest in our super popular ESP32 based Feather boards.
