# Fritzing sketch S3feather_tsl237module1 (saved by Fritzing 1.0.1rc)
breadboards: 1

parts:
  LED2 = DUO LED RG [package="5 mm [THT]"]
  A2 = featherS3

nets:
  N1: LED2.Vout, A2.Pin_21
  N2: LED2.Vin, A2.Pin_2
  N3: LED2.GND, A2.Pin_4, A2.Pin_17, A2.Pin_38
  N4: A2.Pin_19, A2.Pin_20
  N5: A2.Pin_29, A2.Pin_34

notes:
  GND
  Vout
  Vin
  TSL237
  Divider/counter

custom parts:
  DUO LED RG: A 5mm DUO-color LED with red and green inside. Pin order: red - com. cathode - green
  featherS3: FeatherS3 is the latest in our super popular ESP32 based Feather boards.
