# Fritzing sketch S3feather_voltage_divider2 (saved by Fritzing 1.0.1rc)
breadboards: 1

parts:
  BAT1 = 18650 battery holder [package=battery-18650-kit]
  R2 = Resistor [tolerance=±5% resistance=100 package="2512 [SMD]"]
  R1 = Resistor [tolerance=±5% resistance=470 package="2512 [SMD]"]
  A2 = featherS3

nets:
  N1: BAT1.+, R1.Pin_1
  N2: BAT1.-, R2.Pin_0, A2.Pin_4, A2.Pin_17, A2.Pin_20, A2.Pin_38
  N3: R2.Pin_1, R1.Pin_0, A2.Pin_5
  N4: A2.Pin_29, A2.Pin_34, A2.Pin_35

notes:
  R2
  R1
  Vdata
  Vin
  GND

custom parts:
  18650 battery holder: 18650 Battery Holder
  featherS3: FeatherS3 is the latest in our super popular ESP32 based Feather boards.
